# Fritzing sketch Star Pointer v1 (saved by Fritzing 0.9.6b)

parts:
  Driver1 = 28BYJ-48 Driver Module [part_number=ULN2003 package=THT]
  Driver2 = 28BYJ-48 Driver Module [part_number=ULN2003 package=THT]
  Azimuth = 28BYJ-48 Stepper Motor
  Altitude = 28BYJ-48 Stepper Motor
  5V_in = Power Jack [package=power_jack_smd]
  U1 = NodeMCU V3.0

nets:
  N1: Driver1.IN1, U1.D0
  N2: Driver1.IN2, U1.D1
  N3: Driver1.IN3, U1.D2
  N4: Driver1.IN4, U1.D3
  GND: Driver1.GND, Driver2.GND, 5V_in.GNDBREAK, U1.GND
  GND_2: Driver1.Vmotor, Driver2.Vmotor, 5V_in.GND, U1.Vin
  N5: Driver1.blue-pin, Azimuth.BLUE
  N6: Driver1.pink-pin, Azimuth.PINK
  N7: Driver1.yellow-pin, Azimuth.YELLOW
  N8: Driver1.orange-pin, Azimuth.ORANGE
  N9: Driver1.red-pin, Azimuth.RED
  N10: Driver2.IN1, U1.D5
  N11: Driver2.IN2, U1.D6
  N12: Driver2.IN3, U1.D7
  N13: Driver2.IN4, U1.D8
  N14: Driver2.blue-pin, Altitude.BLUE
  N15: Driver2.pink-pin, Altitude.PINK
  N16: Driver2.yellow-pin, Altitude.YELLOW
  N17: Driver2.orange-pin, Altitude.ORANGE
  N18: Driver2.red-pin, Altitude.RED

custom parts:
  28BYJ-48 Driver Module: ULN2003 Driver Module for the 28BYJ-48 Unipolar Stepper Motor LED A - Blue wire - Bottom coil left LED B - Pink wire - Top coil left LED C - Yellow wire - Bottom coil right LED D - Orange wire - Top coil right Common rail - red Connector pins: blue - pink - yellow - orange - red Control pins - IN1 to IN4 Power pins - GND & Vmotor (5-12V) On/Off jumper (if removed, power to motor is cut).
  28BYJ-48 Stepper Motor: 28BYJ-48 gear-reduction stepper motor (small)
  NodeMCU V3.0: ESP8266 based NodeMCU
